# Fritzing sketch Proximity_Sensor_Wiring_Diagram (saved by Fritzing 0.9.5d)
breadboards: 1

parts:
  Part1 = Arduino Uno (Rev3) - ICSP
  HC-SR04_Sensor_1 = HC-SR04 Ultrasonic Distance Sensor
  LED1 = smd LED [color="Green (565nm)" package="0805 [SMD]"]
  LED2 = smd LED [color="Yellow (595nm)" package="0805 [SMD]"]
  LED3 = smd LED [color="Red (633nm)" package="0805 [SMD]"]
  R1 = Resistor [tolerance=±5% resistance=1000 package="0805 [SMD]"]
  R2 = Resistor [tolerance=±5% resistance=1000 package="0805 [SMD]"]
  R3 = Resistor [tolerance=±5% resistance=1000 package="2512 [SMD]"]
  buz1 = Piezo Buzzer

nets:
  N1: Part1.D8, LED3.anode
  N2: Part1.D9_PWM, LED2.anode
  N3: Part1.D10_PWM/SS, LED1.anode
  N4: Part1.D11_PWM/MOSI, buz1.pin_1
  N5: Part1.D12/MISO, HC-SR04_Sensor_1.ECHO
  N6: Part1.D13/SCK, HC-SR04_Sensor_1.TRIG
  5V: Part1.5V, HC-SR04_Sensor_1.VCC
  GND: Part1.GND, HC-SR04_Sensor_1.GND, R1.Pin_0, R2.Pin_0, R3.Pin_0, buz1.pin_2
  N7: LED1.cathode, R3.Pin_1
  N8: LED2.cathode, R2.Pin_1
  N9: LED3.cathode, R1.Pin_1

custom parts:
  Piezo Buzzer: Part from https://www.nutsvolts.com/magazine/article/november2012_SmileysWorkshop. Breadboard and icon images modified to be 0.3" in spacing and be more similar to the actual physical part.
